# Fritzing sketch arduino-countdown-sketch (saved by Fritzing 0.8.3b)
breadboards: 1

parts:
  Part1 = Arduino Uno (Rev3)
  LED1 = 8x8 LED Matrix (green)
  R1 = Resistor [tolerance=±5% resistance=10k package=THT]
  S1 = Pushbutton [package="[THT]"]
  S2 = Pushbutton [package="[THT]"]
  R2 = Resistor [tolerance=±5% resistance=10k package=THT]
  J1 = Piezo Speaker
  R3 = Resistor [tolerance=±5% resistance=220 package=THT]

nets:
  N1: Part1.A4/SDA, LED1.D
  N2: Part1.A5/SCL, LED1.C
  N3: Part1.GND, R1.Pin_0, R2.Pin_0, J1.pin1
  N4: Part1.D8, R3.Pin_0
  N5: Part1.D2, R1.Pin_1, S1.Pin_3, S1.Pin_4
  N6: Part1.D3_PWM, S2.Pin_3, S2.Pin_4, R2.Pin_1
  N7: Part1.5V, LED1.+, LED1.-, S1.Pin_1, S1.Pin_2, S2.Pin_1, S2.Pin_2
  N8: J1.pin2, R3.Pin_1

custom parts:
  8x8 LED Matrix (green): 8x8 LED Matrix with I2C control (green)
